# Fritzing sketch tamrin1 (saved by Fritzing 0.9.4)
breadboards: 1

parts:
  Part1 = Arduino Uno (Rev3) - ICSP
  DI1 = 7-Segment LED Display [package=THT]
  R1 = Resistor [tolerance=±5% resistance=220 package=THT]
  R2 = Resistor [tolerance=±5% resistance=220 package=THT]
  R3 = Resistor [tolerance=±5% resistance=220 package=THT]
  R4 = Resistor [tolerance=±5% resistance=220 package=THT]
  R5 = Resistor [tolerance=±5% resistance=220 package=THT]
  R6 = Resistor [tolerance=±5% resistance=220 package=THT]
  R7 = Resistor [tolerance=±5% resistance=220 package=THT]

nets:
  N1: Part1.D1/TX, R4.Pin_1
  N2: Part1.D2, R3.Pin_1
  N3: Part1.D3_PWM, R7.Pin_1
  N4: Part1.D4, R5.Pin_0
  N5: Part1.D5_PWM, R6.Pin_0
  N6: Part1.D6_PWM, R2.Pin_0
  N7: Part1.D7, R1.Pin_0
  N8: Part1.GND, DI1.commAnode#2
  N9: DI1.cathodeE, R6.Pin_1
  N10: DI1.cathodeD, R5.Pin_1
  N11: DI1.cathodeDP, R7.Pin_0
  N12: DI1.cathodeB, R3.Pin_0
  N13: DI1.cathodeA, R4.Pin_0
  N14: DI1.cathodeF, R2.Pin_1
  N15: DI1.cathodeG, R1.Pin_1
