# Fritzing sketch tamrin4 (saved by Fritzing 0.9.4)
breadboards: 1

parts:
  Part1 = Arduino Uno (Rev3) - ICSP
  R1 = Resistor [tolerance=±5% resistance=220 package=THT]
  R2 = PHOTOCELL [package=photocell-kit]
  LED1 = LED - 3mm [color="Red (633nm)" package="3 mm [THT]"]

nets:
  N1: Part1.A0, R1.Pin_0, R2.P$1
  N2: Part1.D10_PWM/SS, LED1.anode
  N3: Part1.5V, R2.P$2
  N4: Part1.GND, R1.Pin_1, LED1.cathode
