# Fritzing sketch tamrin5 (saved by Fritzing 0.9.4)
breadboards: 1

parts:
  Part1 = Arduino Uno (Rev3) - ICSP
  SP1 = SPEAKER [package=pcb_mount_speaker]
  S1 = Pushbutton [package="[THT]"]

nets:
  N1: Part1.RESET, S1.Pin_1, S1.Pin_2
  N2: Part1.D10_PWM/SS, SP1.-
  N3: Part1.GND, SP1.+, S1.Pin_3, S1.Pin_4
